// Digital circuit 16bit_carry_lookahead_adder.dig as structural Verilog
module _16bit_carry_lookahead_adder (
  input  [15:0] A,
  input  [15:0] B,
  input  subtract,
  input  Ci,
  output [15:0] S,
  output Co
);

  wire and_1_out, and_2_out, and_3_out, and_4_out, and_5_out, and_6_out, and_7_out, and_8_out, and_9_out,
       and_10_out, and_11_out, and_12_out, and_13_out, and_14_out, and_15_out, and_16_out, and_17_out, g_0,
       o_operator_1_g, o_operator_1_p, o_operator_2_g, o_operator_2_p, o_operator_3_g, o_operator_3_p,
       o_operator_4_g, o_operator_4_p, o_operator_5_g, o_operator_5_p, o_operator_6_g, o_operator_6_p,
       o_operator_7_g, o_operator_7_p, o_operator_8_g, o_operator_8_p, o_operator_9_g, o_operator_10_g,
       o_operator_10_p, o_operator_11_g, o_operator_11_p, o_operator_12_g, o_operator_12_p, o_operator_13_g,
       o_operator_13_p, o_operator_14_g, o_operator_15_g, o_operator_15_p, o_operator_16_g, o_operator_16_p,
       o_operator_17_g, o_operator_17_p, o_operator_18_g, o_operator_19_g, o_operator_20_g, o_operator_20_p,
       o_operator_22_g, o_operator_23_g, o_operator_23_p, o_operator_24_g, o_operator_25_g, o_operator_25_p,
       o_operator_26_g, or_1_out, xor_1_out, xor_2_out, xor_3_out, xor_4_out, xor_5_out, xor_6_out,
       xor_7_out, xor_8_out, xor_9_out, xor_10_out, xor_11_out, xor_12_out, xor_13_out, xor_14_out,
       xor_15_out, xor_16_out;
  wire [15:0] multiplexer_2_out, not_1_out;

  Multiplexer multiplexer_1 (.sel(subtract), .in_0(Ci), .in_1(subtract), .out(g_0));
  assign not_1_out = ~B;  // Not not_1, 16 bits wide
  Multiplexer #(.Bits(16)) multiplexer_2 (.sel(subtract), .in_0(B), .in_1(not_1_out), .out(multiplexer_2_out));
  and and_1 (and_1_out, multiplexer_2_out[0], A[0]);
  xor xor_1 (xor_1_out, multiplexer_2_out[0], A[0]);
  and and_2 (and_2_out, multiplexer_2_out[1], A[1]);
  xor xor_2 (xor_2_out, multiplexer_2_out[1], A[1]);
  and and_3 (and_3_out, multiplexer_2_out[2], A[2]);
  xor xor_3 (xor_3_out, multiplexer_2_out[2], A[2]);
  and and_4 (and_4_out, multiplexer_2_out[3], A[3]);
  xor xor_4 (xor_4_out, multiplexer_2_out[3], A[3]);
  and and_5 (and_5_out, multiplexer_2_out[4], A[4]);
  xor xor_5 (xor_5_out, multiplexer_2_out[4], A[4]);
  and and_6 (and_6_out, multiplexer_2_out[5], A[5]);
  xor xor_6 (xor_6_out, multiplexer_2_out[5], A[5]);
  and and_7 (and_7_out, multiplexer_2_out[6], A[6]);
  xor xor_7 (xor_7_out, multiplexer_2_out[6], A[6]);
  and and_8 (and_8_out, multiplexer_2_out[7], A[7]);
  xor xor_8 (xor_8_out, multiplexer_2_out[7], A[7]);
  and and_9 (and_9_out, multiplexer_2_out[8], A[8]);
  xor xor_9 (xor_9_out, multiplexer_2_out[8], A[8]);
  and and_10 (and_10_out, multiplexer_2_out[9], A[9]);
  xor xor_10 (xor_10_out, multiplexer_2_out[9], A[9]);
  and and_11 (and_11_out, multiplexer_2_out[10], A[10]);
  xor xor_11 (xor_11_out, multiplexer_2_out[10], A[10]);
  and and_12 (and_12_out, multiplexer_2_out[11], A[11]);
  xor xor_12 (xor_12_out, multiplexer_2_out[11], A[11]);
  and and_13 (and_13_out, multiplexer_2_out[12], A[12]);
  xor xor_13 (xor_13_out, multiplexer_2_out[12], A[12]);
  and and_14 (and_14_out, multiplexer_2_out[13], A[13]);
  xor xor_14 (xor_14_out, multiplexer_2_out[13], A[13]);
  and and_15 (and_15_out, multiplexer_2_out[14], A[14]);
  xor xor_15 (xor_15_out, multiplexer_2_out[14], A[14]);
  and and_16 (and_16_out, multiplexer_2_out[15], A[15]);
  xor xor_16 (xor_16_out, multiplexer_2_out[15], A[15]);
  and and_17 (and_17_out, g_0, xor_1_out);
  or or_1 (or_1_out, and_1_out, and_17_out);
  o_operator o_operator_1 (
    .g__in(or_1_out), .p__in(xor_1_out), .g_in(and_2_out), .p_in(xor_2_out), .g(o_operator_1_g),
    .p(o_operator_1_p));
  o_operator o_operator_2 (
    .g__in(and_3_out), .p__in(xor_3_out), .g_in(and_4_out), .p_in(xor_4_out), .g(o_operator_2_g),
    .p(o_operator_2_p));
  o_operator o_operator_3 (
    .g__in(and_5_out), .p__in(xor_5_out), .g_in(and_6_out), .p_in(xor_6_out), .g(o_operator_3_g),
    .p(o_operator_3_p));
  o_operator o_operator_4 (
    .g__in(and_7_out), .p__in(xor_7_out), .g_in(and_8_out), .p_in(xor_8_out), .g(o_operator_4_g),
    .p(o_operator_4_p));
  o_operator o_operator_5 (
    .g__in(and_9_out), .p__in(xor_9_out), .g_in(and_10_out), .p_in(xor_10_out), .g(o_operator_5_g),
    .p(o_operator_5_p));
  o_operator o_operator_6 (
    .g__in(and_11_out), .p__in(xor_11_out), .g_in(and_12_out), .p_in(xor_12_out), .g(o_operator_6_g),
    .p(o_operator_6_p));
  o_operator o_operator_7 (
    .g__in(and_13_out), .p__in(xor_13_out), .g_in(and_14_out), .p_in(xor_14_out), .g(o_operator_7_g),
    .p(o_operator_7_p));
  o_operator o_operator_8 (
    .g__in(and_15_out), .p__in(xor_15_out), .g_in(and_16_out), .p_in(xor_16_out), .g(o_operator_8_g),
    .p(o_operator_8_p));
  o_operator o_operator_9 (
    .g__in(o_operator_1_g), .p__in(o_operator_1_p), .g_in(and_3_out), .p_in(xor_3_out), .g(o_operator_9_g));  // open: p
  o_operator o_operator_10 (
    .g__in(o_operator_1_g), .p__in(o_operator_1_p), .g_in(o_operator_2_g), .p_in(o_operator_2_p),
    .g(o_operator_10_g), .p(o_operator_10_p));
  o_operator o_operator_11 (
    .g__in(o_operator_3_g), .p__in(o_operator_3_p), .g_in(o_operator_4_g), .p_in(o_operator_4_p),
    .g(o_operator_11_g), .p(o_operator_11_p));
  o_operator o_operator_12 (
    .g__in(o_operator_5_g), .p__in(o_operator_5_p), .g_in(o_operator_6_g), .p_in(o_operator_6_p),
    .g(o_operator_12_g), .p(o_operator_12_p));
  o_operator o_operator_13 (
    .g__in(o_operator_7_g), .p__in(o_operator_7_p), .g_in(o_operator_8_g), .p_in(o_operator_8_p),
    .g(o_operator_13_g), .p(o_operator_13_p));
  o_operator o_operator_14 (
    .g__in(o_operator_10_g), .p__in(o_operator_10_p), .g_in(and_5_out), .p_in(xor_5_out), .g(o_operator_14_g));  // open: p
  o_operator o_operator_15 (
    .g__in(o_operator_10_g), .p__in(o_operator_10_p), .g_in(o_operator_3_g), .p_in(o_operator_3_p),
    .g(o_operator_15_g), .p(o_operator_15_p));
  o_operator o_operator_16 (
    .g__in(o_operator_10_g), .p__in(o_operator_10_p), .g_in(o_operator_11_g), .p_in(o_operator_11_p),
    .g(o_operator_16_g), .p(o_operator_16_p));
  o_operator o_operator_17 (
    .g__in(o_operator_12_g), .p__in(o_operator_12_p), .g_in(o_operator_13_g), .p_in(o_operator_13_p),
    .g(o_operator_17_g), .p(o_operator_17_p));
  o_operator o_operator_18 (
    .g__in(o_operator_15_g), .p__in(o_operator_15_p), .g_in(and_7_out), .p_in(xor_7_out), .g(o_operator_18_g));  // open: p
  o_operator o_operator_19 (
    .g__in(o_operator_16_g), .p__in(o_operator_16_p), .g_in(and_9_out), .p_in(xor_9_out), .g(o_operator_19_g));  // open: p
  o_operator o_operator_20 (
    .g__in(o_operator_16_g), .p__in(o_operator_16_p), .g_in(o_operator_5_g), .p_in(o_operator_5_p),
    .g(o_operator_20_g), .p(o_operator_20_p));
  o_operator o_operator_21 (
    .g__in(o_operator_16_g), .p__in(o_operator_16_p), .g_in(o_operator_17_g), .p_in(o_operator_17_p), .g(Co));  // open: p
  o_operator o_operator_22 (
    .g__in(o_operator_20_g), .p__in(o_operator_20_p), .g_in(and_11_out), .p_in(xor_11_out),
    .g(o_operator_22_g));  // open: p
  o_operator o_operator_23 (
    .g__in(o_operator_20_g), .p__in(o_operator_20_p), .g_in(o_operator_12_g), .p_in(o_operator_12_p),
    .g(o_operator_23_g), .p(o_operator_23_p));
  o_operator o_operator_24 (
    .g__in(o_operator_23_g), .p__in(o_operator_23_p), .g_in(and_13_out), .p_in(xor_13_out),
    .g(o_operator_24_g));  // open: p
  o_operator o_operator_25 (
    .g__in(o_operator_23_g), .p__in(o_operator_23_p), .g_in(o_operator_7_g), .p_in(o_operator_7_p),
    .g(o_operator_25_g), .p(o_operator_25_p));
  o_operator o_operator_26 (
    .g__in(o_operator_25_g), .p__in(o_operator_25_p), .g_in(and_15_out), .p_in(xor_15_out),
    .g(o_operator_26_g));  // open: p
  xor xor_17 (S[0], g_0, xor_1_out);
  xor xor_18 (S[1], or_1_out, xor_2_out);
  xor xor_19 (S[2], o_operator_1_g, xor_3_out);
  xor xor_20 (S[3], o_operator_9_g, xor_4_out);
  xor xor_21 (S[4], o_operator_10_g, xor_5_out);
  xor xor_22 (S[5], o_operator_14_g, xor_6_out);
  xor xor_23 (S[6], o_operator_15_g, xor_7_out);
  xor xor_24 (S[7], o_operator_18_g, xor_8_out);
  xor xor_25 (S[8], o_operator_16_g, xor_9_out);
  xor xor_26 (S[9], o_operator_19_g, xor_10_out);
  xor xor_27 (S[10], o_operator_20_g, xor_11_out);
  xor xor_28 (S[11], o_operator_22_g, xor_12_out);
  xor xor_29 (S[12], o_operator_23_g, xor_13_out);
  xor xor_30 (S[13], o_operator_24_g, xor_14_out);
  xor xor_31 (S[14], o_operator_25_g, xor_15_out);
  xor xor_32 (S[15], o_operator_26_g, xor_16_out);

  // Other names for the same wires on the sheet: C_out = Co

  // Notes on the sheet:
  //   Todo
  //   1
  //   2
  //   3
  //   4
  //   5
  //   6
  //   7
  //   8
  //   9
  //   10
  //   11
  //   12
  //   13
  //   14
  //   15
  //   16
  //   g
  //   p
  //   S1
  //   S2
  //   S3
  //   S4
  //   S5
  //   S6
  //   S7
  //   S8
  //   S9
  //   S10
  //   S11
  //   S12
  //   S13
  //   S14
  //   S15
  //   S16
endmodule

/* Test case Adder/Subtractor:
# Add and subract test case

A B subtract Ci S Co

(1) (1)  0  0 (2) ((2)>255)

loop(a,100)
	loop(b,16)
		(a) (b)  0  0 (a+b) ((a+b)>65536)
		(a) (b)  0  1 (a+b+1) ((a+b+1)>65536)
		(a) (b)  1  1 (a-b) (a>b-1)
	end loop
end loop
*/
