// Digital circuit 1bit_ALU.dig as structural Verilog
module _1bit_ALU (
  input  A,
  input  B,
  input  Ainvert,
  input  Bnegate,
  input  CarryIn,
  input  [2:0] Operation,
  input  Less,
  output Result,
  output CarryOut,
  output Set
);

  wire and_1_out, multiplexer_1_out, multiplexer_2_out, not_1_out, not_2_out, or_1_out;

  not not_1 (not_1_out, A);
  Multiplexer multiplexer_1 (.sel(Ainvert), .in_0(A), .in_1(not_1_out), .out(multiplexer_1_out));
  not not_2 (not_2_out, B);
  Multiplexer multiplexer_2 (.sel(Bnegate), .in_0(B), .in_1(not_2_out), .out(multiplexer_2_out));
  and and_1 (and_1_out, multiplexer_1_out, multiplexer_2_out);
  or or_1 (or_1_out, multiplexer_1_out, multiplexer_2_out);
  Add Adder (.a(multiplexer_1_out), .b(multiplexer_2_out), .c_i(CarryIn), .s(Less), .c_o(CarryOut));
  Multiplexer #(.Selector_Bits(3)) multiplexer_3 (
    .sel(Operation), .in_0(and_1_out), .in_1(or_1_out), .in_2(Less), .in_3(Less), .in_4(1'b1), .in_5(1'b1),
    .in_6(1'b1), .in_7(1'b1), .out(Result));

  assign Set = Less;
endmodule
