// Digital circuit 8_Dadda_mult.dig as structural Verilog
module _8_Dadda_mult (
  input  [7:0] A,
  input  [7:0] B
);

  wire [7:0] and_1_out, and_2_out, and_3_out, and_4_out, and_5_out, and_6_out, and_7_out, and_8_out,
       multiplexer_1_out, multiplexer_2_out, multiplexer_3_out, multiplexer_4_out, multiplexer_5_out,
       multiplexer_6_out, multiplexer_7_out, multiplexer_8_out;

  Multiplexer #(.Bits(8)) multiplexer_1 (.sel(B[0]), .in_0({8{1'b0}}), .in_1({8{1'b1}}), .out(multiplexer_1_out));
  Multiplexer #(.Bits(8)) multiplexer_2 (.sel(B[1]), .in_0({8{1'b0}}), .in_1({8{1'b1}}), .out(multiplexer_2_out));
  Multiplexer #(.Bits(8)) multiplexer_3 (.sel(B[2]), .in_0({8{1'b0}}), .in_1({8{1'b1}}), .out(multiplexer_3_out));
  Multiplexer #(.Bits(8)) multiplexer_4 (.sel(B[3]), .in_0({8{1'b0}}), .in_1({8{1'b1}}), .out(multiplexer_4_out));
  Multiplexer #(.Bits(8)) multiplexer_5 (.sel(B[4]), .in_0({8{1'b0}}), .in_1({8{1'b1}}), .out(multiplexer_5_out));
  Multiplexer #(.Bits(8)) multiplexer_6 (.sel(B[5]), .in_0({8{1'b0}}), .in_1({8{1'b1}}), .out(multiplexer_6_out));
  Multiplexer #(.Bits(8)) multiplexer_7 (.sel(B[6]), .in_0({8{1'b0}}), .in_1({8{1'b1}}), .out(multiplexer_7_out));
  Multiplexer #(.Bits(8)) multiplexer_8 (.sel(B[7]), .in_0({8{1'b0}}), .in_1({8{1'b1}}), .out(multiplexer_8_out));
  assign and_1_out = multiplexer_1_out & A;  // And and_1, 8 bits wide
  assign and_2_out = multiplexer_2_out & A;  // And and_2, 8 bits wide
  assign and_3_out = multiplexer_3_out & A;  // And and_3, 8 bits wide
  assign and_4_out = multiplexer_4_out & A;  // And and_4, 8 bits wide
  assign and_5_out = multiplexer_5_out & A;  // And and_5, 8 bits wide
  assign and_6_out = multiplexer_6_out & A;  // And and_6, 8 bits wide
  assign and_7_out = multiplexer_7_out & A;  // And and_7, 8 bits wide
  assign and_8_out = multiplexer_8_out & A;  // And and_8, 8 bits wide

  // Other names for the same wires on the sheet: B_0 = B[0]; B_1 = B[1]; B_2 = B[2]; B_3 = B[3]; B_4 = B[4];
  //   B_5 = B[5]; B_6 = B[6]; B_7 = B[7]
endmodule
