// Digital circuit 8_and.dig as structural Verilog
module _8_and (
  input  [7:0] A,
  input  [7:0] B,
  output [7:0] Y
);

  and and_1 (Y[0], A[0], B[0]);
  and and_2 (Y[1], A[1], B[1]);
  and and_3 (Y[2], A[2], B[2]);
  and and_4 (Y[3], A[3], B[3]);
  and and_5 (Y[4], A[4], B[4]);
  and and_6 (Y[5], A[5], B[5]);
  and and_7 (Y[6], A[6], B[6]);
  and and_8 (Y[7], A[7], B[7]);
endmodule

/* Test case AND Test:
# 8 Bit Adder circuit test

A B Y

loop(a,256)
	loop(b,256)
		(a) (b) (a&b)
	end loop
end loop
*/
