// Digital circuit 8_full_adder.dig as structural Verilog
module _8_full_adder (
  input  [7:0] A,
  input  [7:0] B,
  input  Carry_in,
  input  subtract,
  output [7:0] Y,
  output C_arry
);

  wire full_adder_1_carry_out, full_adder_2_carry_out, full_adder_3_carry_out, full_adder_4_carry_out,
       full_adder_5_carry_out, full_adder_6_carry_out, full_adder_7_carry_out, xor_1_out, xor_2_out,
       xor_3_out, xor_4_out, xor_5_out, xor_6_out, xor_7_out, xor_8_out;

  xor xor_1 (xor_1_out, B[0], subtract);
  xor xor_2 (xor_2_out, B[1], subtract);
  xor xor_3 (xor_3_out, B[2], subtract);
  xor xor_4 (xor_4_out, B[3], subtract);
  xor xor_5 (xor_5_out, B[4], subtract);
  xor xor_6 (xor_6_out, B[5], subtract);
  xor xor_7 (xor_7_out, B[6], subtract);
  xor xor_8 (xor_8_out, B[7], subtract);
  full_adder full_adder_1 (.Carry_in(Carry_in), .Carry_out(full_adder_1_carry_out), .Y(Y[0]), .A(A[0]), .B(xor_1_out));
  full_adder full_adder_2 (
    .Carry_in(full_adder_1_carry_out), .Carry_out(full_adder_2_carry_out), .Y(Y[1]), .A(A[1]), .B(xor_2_out));
  full_adder full_adder_3 (
    .Carry_in(full_adder_2_carry_out), .Carry_out(full_adder_3_carry_out), .Y(Y[2]), .A(A[2]), .B(xor_3_out));
  full_adder full_adder_4 (
    .Carry_in(full_adder_3_carry_out), .Carry_out(full_adder_4_carry_out), .Y(Y[3]), .A(A[3]), .B(xor_4_out));
  full_adder full_adder_5 (
    .Carry_in(full_adder_4_carry_out), .Carry_out(full_adder_5_carry_out), .Y(Y[4]), .A(A[4]), .B(xor_5_out));
  full_adder full_adder_6 (
    .Carry_in(full_adder_5_carry_out), .Carry_out(full_adder_6_carry_out), .Y(Y[5]), .A(A[5]), .B(xor_6_out));
  full_adder full_adder_7 (
    .Carry_in(full_adder_6_carry_out), .Carry_out(full_adder_7_carry_out), .Y(Y[6]), .A(A[6]), .B(xor_7_out));
  full_adder full_adder_8 (.Carry_in(full_adder_7_carry_out), .Carry_out(C_arry), .Y(Y[7]), .A(A[7]), .B(xor_8_out));
  // Probe on Y

  // Other names for the same wires on the sheet: sub = subtract
endmodule

/* Test case Full adder test:
# Add and subract test case

A B subtract Carry_in Y C(arry)

loop(a,256)
	loop(b,256)
		(a) (b)  0  0 (a+b) ((a+b)>255)
		(a) (b)  0  1 (a+b+1) ((a+b+1)>255)
		(a) (b)  1  0 (a-b-1) (a>b)
		(a) (b)  1  1 (a-b) (a>b-1)
	end loop
end loop
*/
