// Digital circuit 8_or.dig as structural Verilog
module _8_or (
  input  [7:0] A,
  input  [7:0] B,
  output [7:0] Y
);

  or or_1 (Y[0], A[0], B[0]);
  or or_2 (Y[1], A[1], B[1]);
  or or_3 (Y[2], A[2], B[2]);
  or or_4 (Y[3], A[3], B[3]);
  or or_5 (Y[4], A[4], B[4]);
  or or_6 (Y[5], A[5], B[5]);
  or or_7 (Y[6], A[6], B[6]);
  or or_8 (Y[7], A[7], B[7]);
endmodule

/* Test case:
A B Y 

loop(a,256)
	loop(b,256)
		(a) (b) (a | b)
	end loop
end loop
*/
