// Digital circuit BranchConditions.dig as structural Verilog
module BranchConditions (
  input  [2:0] func3,
  input  BranchE,
  input  [3:0] NZCV,
  output Y
);

  wire and_1_out, and_2_out, and_3_out, and_4_out, and_5_out, and_6_out, and_7_out, and_8_out, and_9_out,
       and_10_out, and_11_out, and_12_out, and_13_out, and_14_out, and_15_out, and_16_out, and_17_out,
       and_18_out, and_19_out, and_20_out, and_21_out, and_22_out, and_23_out, and_24_out, not_1_out,
       not_2_out, not_3_out, not_4_out, not_5_out, not_6_out, not_7_out, or_1_out, or_2_out, or_3_out,
       or_4_out, or_5_out, or_6_out, or_7_out;

  not not_1 (not_1_out, func3[2]);
  not not_2 (not_2_out, func3[1]);
  not not_3 (not_3_out, func3[0]);
  not not_4 (not_4_out, NZCV[2]);
  not not_5 (not_5_out, NZCV[0]);
  not not_6 (not_6_out, NZCV[3]);
  not not_7 (not_7_out, NZCV[1]);
  and and_1 (and_1_out, not_4_out, not_3_out);
  and and_2 (and_2_out, NZCV[2], func3[0]);
  and and_3 (and_3_out, not_3_out, not_2_out);
  and and_4 (and_4_out, not_5_out, NZCV[3]);
  and and_5 (and_5_out, not_3_out, not_2_out);
  and and_6 (and_6_out, NZCV[0], not_6_out);
  and and_7 (and_7_out, func3[0], not_2_out);
  and and_8 (and_8_out, not_5_out, not_6_out);
  and and_9 (and_9_out, func3[0], not_2_out);
  and and_10 (and_10_out, NZCV[0], NZCV[3]);
  and and_11 (and_11_out, not_3_out, not_1_out);
  and and_12 (and_12_out, func3[0], not_1_out);
  and and_13 (and_13_out, and_1_out, func3[1]);
  and and_14 (and_14_out, and_2_out, func3[1]);
  and and_15 (and_15_out, and_3_out, func3[2]);
  and and_16 (and_16_out, and_5_out, func3[2]);
  and and_17 (and_17_out, and_7_out, func3[2]);
  and and_18 (and_18_out, and_9_out, func3[2]);
  and and_19 (and_19_out, and_11_out, NZCV[1]);
  and and_20 (and_20_out, and_12_out, not_7_out);
  or or_1 (or_1_out, and_13_out, and_14_out);
  and and_21 (and_21_out, and_15_out, and_4_out);
  and and_22 (and_22_out, and_16_out, and_6_out);
  and and_23 (and_23_out, and_17_out, and_8_out);
  and and_24 (and_24_out, and_18_out, and_10_out);
  or or_2 (or_2_out, and_19_out, and_20_out);
  or or_3 (or_3_out, and_21_out, and_22_out);
  or or_4 (or_4_out, and_23_out, and_24_out);
  or or_5 (or_5_out, or_1_out, or_3_out);
  or or_6 (or_6_out, or_4_out, or_2_out);
  or or_7 (or_7_out, or_5_out, or_6_out);
  and and_25 (Y, or_7_out, BranchE);
  // Pins of 1 and 4 bits meet at NZCV

  // Other names for the same wires on the sheet: func3_0 = func3[0]; func3_1 = func3[1]; func3_2 = func3[2];
  //   negative = NZCV[0]; zero = NZCV[1]; carry = NZCV[2]; overflow = NZCV[3]
endmodule
