// Digital circuit CPU.dig as structural Verilog
module CPU (
  input  CLK
);

  wire not_1_out, PC_ovf;
  wire [31:0] PC_out, ramsingleportsel_1_d;

  Counter #(.Bits(32), .isProgramCounter("true")) PC (.en(1'b1), .C(CLK), .clr(PC_ovf), .out(PC_out), .ovf(PC_ovf));
  not not_1 (not_1_out, PC_out[31]);
  RAMSinglePortSel #(.AddrBits(16), .Bits(32)) ramsingleportsel_1 (
    .A(PC_out[15:0]), .CS(1'b1), .WE(1'b0), .OE(not_1_out), .D(ramsingleportsel_1_d));
  RAMSinglePortSel #(.AddrBits(16), .Bits(32)) ramsingleportsel_2 (
    .A(PC_out[31:16]), .CS(1'b1), .WE(1'b0), .OE(PC_out[31]), .D(ramsingleportsel_1_d));
  instruction_decoder instruction_decoder_1 ();  // open: Instruction, Zero, PCWrite, ALUControl, ALUSrcA, ALUSrcB, ResultSrc, ImmSrc, AdrSrc, IRWrite, MemWrite, RegWrite, CLK

  // Notes on the sheet:
  //   CLK: Hz: 100
  //   0-24 Field information
  //   25-31 Instruction type (R,I,U,J-S, etc)
endmodule
