// Digital circuit CU_Pipelined.dig as structural Verilog
module CU_Pipelined (
  input  [31:0] Instruction,
  output RegWrite,
  output [1:0] ResultSrc,
  output MemWrite,
  output Jump,
  output Branch,
  output [2:0] ALUControl,
  output ALUSrc,
  output [2:0] ImmSrc,
  output [2:0] func3
);

  wire and_1_out, and_2_out, and_3_out, and_4_out, and_5_out, and_6_out, and_7_out, and_8_out, and_9_out,
       and_10_out, and_11_out, and_12_out, and_13_out, and_14_out, and_15_out, and_16_out, and_17_out,
       and_18_out, and_19_out, and_20_out, not_1_out, not_2_out, not_3_out, not_4_out, not_5_out, not_6_out,
       not_7_out, not_8_out, not_9_out, not_10_out, or_1_out, or_2_out, or_3_out, or_4_out, or_8_out;
  wire [2:0] ALU;

  not not_1 (not_1_out, Instruction[14]);
  not not_2 (not_2_out, Instruction[13]);
  not not_3 (not_3_out, Instruction[12]);
  not not_4 (not_4_out, Instruction[5]);
  not not_5 (not_5_out, Instruction[30]);
  and and_1 (and_1_out, Instruction[12], not_1_out);
  and and_2 (and_2_out, not_3_out, not_2_out);
  and and_3 (and_3_out, Instruction[13], not_1_out);
  and and_4 (and_4_out, Instruction[12], not_2_out);
  and and_5 (and_5_out, not_3_out, Instruction[14]);
  and and_6 (and_6_out, Instruction[13], Instruction[14]);
  and and_7 (and_7_out, not_3_out, not_1_out);
  and and_8 (and_8_out, Instruction[30], Instruction[5]);
  and and_9 (and_9_out, not_3_out, Instruction[14]);
  and and_10 (and_10_out, not_3_out, Instruction[14]);
  and and_11 (and_11_out, not_3_out, Instruction[13]);
  and and_12 (and_12_out, and_2_out, Instruction[14]);
  and and_13 (and_13_out, and_4_out, not_1_out);
  and and_14 (and_14_out, and_7_out, and_8_out);
  and and_15 (and_15_out, and_9_out, not_5_out);
  and and_16 (and_16_out, and_10_out, not_4_out);
  or or_1 (or_1_out, and_1_out, and_12_out);
  or or_2 (or_2_out, and_13_out, and_5_out);
  or or_3 (or_3_out, and_14_out, and_15_out);
  or or_4 (or_4_out, and_16_out, and_11_out);
  Multiplexer #(.Selector_Bits(2), .Bits(3)) multiplexer_1 (
    .sel({Instruction[4], Instruction[6]}), .in_0(3'b000), .in_1(3'b001), .in_2(ALU), .in_3(3'b111),
    .out(ALUControl));
  or or_5 (ALU[2], or_1_out, and_3_out);
  or or_6 (ALU[1], or_2_out, and_6_out);
  or or_7 (ALU[0], or_3_out, or_4_out);
  not not_6 (not_6_out, Instruction[6]);
  not not_7 (not_7_out, Instruction[5]);
  not not_8 (not_8_out, Instruction[4]);
  not not_9 (not_9_out, Instruction[3]);
  not not_10 (not_10_out, Instruction[2]);
  or or_8 (or_8_out, Instruction[2], Instruction[4]);
  and and_17 (and_17_out, Instruction[5], not_6_out);
  and and_18 (and_18_out, not_8_out, not_6_out);
  and and_19 (and_19_out, not_8_out, Instruction[5]);
  and and_20 (and_20_out, not_8_out, not_7_out);
  and and_21 (Branch, not_10_out, Instruction[6]);
  or or_9 (RegWrite, or_8_out, not_7_out);
  or or_10 (ImmSrc[0], Instruction[2], and_17_out);
  or or_11 (ALUSrc, and_18_out, not_7_out);
  and and_22 (MemWrite, and_19_out, not_6_out);
  and and_23 (ResultSrc[0], and_20_out, Instruction[1]);
  // Pins of 1 and 3 bits meet at Instruction[14:12]

  assign func3 = Instruction[14:12];
  assign ImmSrc[2:1] = {1'b0, Instruction[6]};
  assign Jump = Instruction[2];
  assign ResultSrc[1] = Instruction[2];

  // Other names for the same wires on the sheet: ALUControl_0 = ALU[0]; ALUControl_1 = ALU[1]; ALUControl_2 = ALU[2];
  //   ImmSrc_0 = ImmSrc[0]; op_0 = Instruction[0]; op_1 = Instruction[1]; op_2 = Instruction[2];
  //   ResultSrc_1 = Instruction[2]; op_3 = Instruction[3]; ALUOp[1:0] = {Instruction[4], Instruction[6]};
  //   ALUOp_1 = Instruction[4]; op_4 = Instruction[4]; op_5 = Instruction[5]; ALUOp_0 = Instruction[6];
  //   ImmSrc_1 = Instruction[6]; op_6 = Instruction[6]; func3_0 = Instruction[12]; func3_1 = Instruction[13];
  //   func3_2 = Instruction[14]; func7_5 = Instruction[30]; ResultSrc_0 = ResultSrc[0]

  // Notes on the sheet:
  //   Instruction: default 4265741027
  //   ALU Decoder
  //   0x1ACCC33
  //   0xFE420AE3
endmodule

/* Test case:
opcode RegWrite ImmSrc ALUSrc MemWrite ALUControl    Branch Jump ResultSrc 


declare opcode = Instruction&0x7F;

0b0000011 
*/
