// Digital circuit Hazard_Unit.dig as structural Verilog
module Hazard_Unit (
  input  [1:0] ResultSrcE,
  input  [4:0] RdM,
  input  [4:0] RdW,
  input  RegWriteM,
  input  RegWriteW,
  input  [4:0] Rs1D,
  input  [4:0] Rs2D,
  input  [4:0] Rs1E,
  input  [4:0] Rs2E,
  input  [4:0] RdE,
  input  PCSrcE,
  output [1:0] ForwardAE,
  output [1:0] ForwardBE,
  output StallF,
  output StallD,
  output FlushD,
  output FlushE
);

  wire and_2_out, and_4_out, nor_1_out, nor_2_out, nor_3_out, nor_4_out, nor_5_out, nor_6_out, not_1_out,
       not_2_out, or_2_out, or_3_out, or_4_out;
  wire [4:0] xor_1_out, xor_2_out, xor_3_out, xor_4_out, xor_5_out, xor_6_out;

  LED led_1 (.in(ResultSrcE[1]));
  assign xor_1_out = Rs1E ^ RdM;  // XOr xor_1, 5 bits wide
  assign xor_2_out = Rs1E ^ RdW;  // XOr xor_2, 5 bits wide
  assign xor_3_out = Rs2E ^ RdM;  // XOr xor_3, 5 bits wide
  assign xor_4_out = Rs2E ^ RdW;  // XOr xor_4, 5 bits wide
  assign xor_5_out = Rs1D ^ RdE;  // XOr xor_5, 5 bits wide
  assign xor_6_out = Rs2D ^ RdE;  // XOr xor_6, 5 bits wide
  or or_1 (FlushE, StallD, PCSrcE);
  nor nor_1 (nor_1_out, xor_1_out[0], xor_1_out[1], xor_1_out[2], xor_1_out[3], xor_1_out[4]);
  or or_2 (or_2_out, Rs1E[0], Rs1E[1], Rs1E[2], Rs1E[3], Rs1E[4]);
  nor nor_2 (nor_2_out, xor_2_out[0], xor_2_out[1], xor_2_out[2], xor_2_out[3], xor_2_out[4]);
  nor nor_3 (nor_3_out, xor_3_out[0], xor_3_out[1], xor_3_out[2], xor_3_out[3], xor_3_out[4]);
  or or_3 (or_3_out, Rs2E[0], Rs2E[1], Rs2E[2], Rs2E[3], Rs2E[4]);
  nor nor_4 (nor_4_out, xor_4_out[0], xor_4_out[1], xor_4_out[2], xor_4_out[3], xor_4_out[4]);
  nor nor_5 (nor_5_out, xor_5_out[0], xor_5_out[1], xor_5_out[2], xor_5_out[3], xor_5_out[4]);
  nor nor_6 (nor_6_out, xor_6_out[0], xor_6_out[1], xor_6_out[2], xor_6_out[3], xor_6_out[4]);
  and and_1 (ForwardAE[1], RegWriteM, nor_1_out, or_2_out);
  and and_2 (and_2_out, or_2_out, nor_2_out, RegWriteW);
  and and_3 (ForwardBE[1], RegWriteM, nor_3_out, or_3_out);
  and and_4 (and_4_out, or_3_out, nor_4_out, RegWriteW);
  or or_4 (or_4_out, nor_5_out, nor_6_out);
  and and_5 (StallD, or_4_out, ResultSrcE[0]);
  not not_1 (not_1_out, ForwardAE[1]);
  not not_2 (not_2_out, ForwardBE[1]);
  and and_6 (ForwardAE[0], not_1_out, and_2_out);
  and and_7 (ForwardBE[0], not_2_out, and_4_out);

  assign FlushD = PCSrcE;
  assign StallF = StallD;

  // Other names for the same wires on the sheet: lwStall = StallD; ResultSrcE_0 = ResultSrcE[0]

  // Notes on the sheet:
  //   ResultSrcE: default 1
  //   RdM: default 5
  //   RdW: default 5
  //   RegWriteM: default 1
  //   RegWriteW: default 1
  //   Rs1D: default 3
  //   Rs2D: default 4
  //   Rs1E: default 5
  //   Rs2E: default 7
  //   RdE: default 16
  //   ForwardAE = 01
  //   else ForwardAE == 00
  //   ForwardBE = 10
  //   ForwardBE = 01
  //   else ForwardBE == 00
  //   ForwardAE = 10
endmodule

/* Test case Stall/Flush test:
# This is a test case for the Hazard Unit

Rs1D Rs2D Rs2E Rs1E RdE PCSrcE ResultSrcE RdM RegWriteM RdW RegWriteW ForwardAE ForwardBE StallD StallF FlushD FlushE


loop(rde,8)
	loop(rs1d,8)
		loop(rs2d,8)
			let lwStall0 = ite(rs1d=rde| rs2d = rde,1,0);

			# Check When ResultSrcE0 is true
			(rs1d) (rs2d) x x (rde) x 1 x x x x x x (lwStall0) (lwStall0) x x
			# Check when ResultScrE0 is false
			(rs1d) (rs2d) x x (rde) x 0 x x x x x x 0 0 x x
			
			# FlushD check
			x x x x x 1 x x x x x x x x x 1 x
			x x x x x 0 x x x x x x x x x 0 x
			
			#FlushE
			# Check When ResultSrcE0 is true
			(rs1d) (rs2d) x x (rde) 1 1 x x x x x x x x x 1
			# Check when ResultScrE0 is false
			(rs1d) (rs2d) x x (rde) 1 0 x x x x x x x x x 1
			# Now PCSrcE is false
			# Check When ResultSrcE0 is true
			(rs1d) (rs2d) x x (rde) 0 1 x x x x x x x x x (lwStall0)
			# Check when ResultScrE0 is false
			(rs1d) (rs2d) x x (rde) 0 0 x x x x x x x x x 0
			
		end loop 
	end loop
end loop
*/

/* Test case Forward Test:
# This is a test case for the Hazard Unit

Rs1D Rs2D Rs2E Rs1E RdE PCSrcE ResultSrcE RdM RegWriteM RdW RegWriteW ForwardAE ForwardBE StallF StallD FlushD FlushE

loop(rdw,32)
	loop(rdm,32)
		loop(regwritem,1)
			loop(regwritew,1)
				loop(rsXe,32)
					let FXE1 = ite(((rsXe = rdm) & regwritem) & (rsXe != 0),1,0);
					let FXE0 = ite(((rsXe = rdw) & regwritew) & (rsXe != 0),1,0);
					let FXE = ite(FXE1,10,FXE0);
					x x (rsXe) (rsXe) x x x (rdm) (regwritem) (rdw) (regwritew) (FXE) (FXE) x x x x
				end loop
			end loop
		end loop
	end loop
end loop
*/
