// Digital circuit Multicycleprocessor.dig as structural Verilog
module Multicycleprocessor (
  input  Clock,
  input  Stop
);

  wire AdrSrc, and_1_out, CLK, IRWrite, MemWrite, not_1_out, PCWrite, RegWrite, reset_1_out;
  wire [1:0] ALUSrcA, ALUSrcB, ImmSrc, ResultSrc;
  wire [2:0] ALUControl;
  wire [3:0] alu_1_nzcv_flags;
  wire [4:0] IR_q_2, IR_q_4;
  wire [6:0] IR_q;
  wire [24:5] IR_q_3;
  wire [31:0] A_q, alu_1_out, ALUOut_q, Data_Register_q, multiplexer_1_out, multiplexer_2_out,
       multiplexer_3_out, multiplexer_4_out, Old_PC_q, PC_q, ramdualport_1_d, Register_File_da,
       Register_File_db, sign_extension_1_immext, WriteData_q;

  and and_1 (and_1_out, PCWrite, reset_1_out);
  Reset reset_1 (.out(reset_1_out));
  // Probe PCNext on multiplexer_4_out
  Register #(.Bits(32), .isProgramCounter("true")) PC (.D(multiplexer_4_out), .C(CLK), .en(and_1_out), .Q(PC_q));
  // Probe PC on PC_q
  Multiplexer #(.Bits(32)) multiplexer_1 (.sel(AdrSrc), .in_0(PC_q), .in_1(multiplexer_4_out), .out(multiplexer_1_out));
  RAMDualPort #(.AddrBits(24), .isProgramMemory("true"), .Bits(32)) ramdualport_1 (
    .A(multiplexer_1_out[23:0]), .Din(WriteData_q), .str(MemWrite), .C(CLK), .ld(1'b1), .D(ramdualport_1_d));
  Register #(.Bits(32)) Old_PC (.D(PC_q), .C(CLK), .en(IRWrite), .Q(Old_PC_q));
  Register #(.Bits(32)) IR (
    .D(ramdualport_1_d), .C(CLK), .en(IRWrite), .Q({IR_q_3[24:13], IR_q_4, IR_q_3[7:5], IR_q_2, IR_q}));
  Register #(.Bits(32)) Data_Register (.D(ramdualport_1_d), .C(CLK), .en(CLK), .Q(Data_Register_q));
  and and_2 (CLK, ~Stop, Clock);  // And
  instruction_decoder instruction_decoder_1 (
    .Instruction({IR_q_3[24:13], IR_q_4, IR_q_3[7:5], IR_q_2, IR_q}), .Zero(alu_1_nzcv_flags[1]),
    .PCWrite(PCWrite), .ALUControl(ALUControl), .ALUSrcA(ALUSrcA), .ALUSrcB(ALUSrcB), .ResultSrc(ResultSrc),
    .ImmSrc(ImmSrc), .AdrSrc(AdrSrc), .IRWrite(IRWrite), .MemWrite(MemWrite), .RegWrite(RegWrite), .CLK(CLK));
  not not_1 (not_1_out, CLK);
  LED led_1 (.in(not_1_out));
  RegisterFile #(.AddrBits(5), .Bits(32)) Register_File (
    .Din(multiplexer_4_out), .we(RegWrite), .Rw(IR_q_2), .C(CLK), .Ra(IR_q_4), .Rb(IR_q_3[17:13]),
    .Da(Register_File_da), .Db(Register_File_db));
  sign_Extension sign_extension_1 (
    .Input({IR_q_3[24:13], IR_q_4, IR_q_3[7:5], IR_q_2}), .ImmSrc(ImmSrc), .ImmExt(sign_extension_1_immext));
  Register #(.Bits(32)) A (.D(Register_File_da), .C(CLK), .en(CLK), .Q(A_q));
  Register #(.Bits(32)) WriteData (.D(Register_File_db), .C(CLK), .en(CLK), .Q(WriteData_q));
  Multiplexer #(.Selector_Bits(2), .Bits(32)) multiplexer_2 (
    .sel(ALUSrcA), .in_0(PC_q), .in_1(Old_PC_q), .in_2(A_q), .in_3({32{1'b0}}), .out(multiplexer_2_out));
  Multiplexer #(.Selector_Bits(2), .Bits(32)) multiplexer_3 (
    .sel(ALUSrcB), .in_0(WriteData_q), .in_1(sign_extension_1_immext), .in_2(32'h4), .in_3({32{1'b0}}),
    .out(multiplexer_3_out));
  ALU alu_1 (
    .ALUControl(ALUControl), .A(multiplexer_2_out), .B(multiplexer_3_out), .OUT(alu_1_out),
    .NZCV_Flags(alu_1_nzcv_flags));
  Register #(.Bits(32)) ALUOut (.D(alu_1_out), .C(CLK), .en(CLK), .Q(ALUOut_q));
  Multiplexer #(.Selector_Bits(2), .Bits(32)) multiplexer_4 (
    .sel(ResultSrc), .in_0(ALUOut_q), .in_1(Data_Register_q), .in_2(alu_1_out), .in_3({32{1'b0}}),
    .out(multiplexer_4_out));

  // Notes on the sheet:
  //   Clock: Hz: 10
endmodule
