// Digital circuit PipelinedProcessor.dig as structural Verilog
module PipelinedProcessor (
  input  Clock,
  input  Stop,
  input  Step,
  output [31:0] out_2
);

  wire _32adder_1_c_o, _32adder_2_c_o, ALUControlE_p5, ALUSrcE_q, and_1_out, branchconditions_1_p3,
       branchconditions_1_p4, BranchE_q, CLK, counter_1_ovf, cu_pipelined_1_p2, cu_pipelined_1_p4,
       cu_pipelined_1_p5, cu_pipelined_1_p6, cu_pipelined_1_p8, cu_pipelined_1_p10, FlushD, FlushE,
       hazard_unit_1_stalld, hazard_unit_1_stallf, JumpE_q, MemWrite, MemWriteE_q, not_1_out, not_2_out,
       not_3_out, not_4_out, PCSrcE, RegWriteE_q, RegWriteM_q, RegWriteW;
  wire [1:0] cu_pipelined_1_p3, hazard_unit_1_forwardae, hazard_unit_1_forwardbe, ResultSrcE_q, ResultSrcM_q,
       ResultSrcW_q;
  wire [2:0] ALUControl, cu_pipelined_1_p7, ImmSrc;
  wire [4:0] RdE_q, RdM_q, RdW_q, Rs1E_q, Rs2E_q;
  wire [23:0] barrelshifter_2_out;
  wire [31:0] _32adder_1_out, _32adder_2_out, alu_1_p4, ALUResultM_q, ALUResultW_q, counter_1_out, Decode,
       Execute, Fetch, ImmExtE_q, InstrD_q, Memory, multiplexer_1_out, multiplexer_2_out, multiplexer_3_out,
       multiplexer_4_out, multiplexer_5_out, myram_1_d, PC_q, PCD_q, PCE_q, PCPlus4D_q, PCPlus4E_q,
       PCPlus4M_q, PCPlus4W_q, ramdualport_1_d, RD1E_q, RE2E_q, ReadDataW_q, Register_File_da,
       Register_File_db, rom_1_d, sign_extension_1_immext, WriteBack, WriteDataM_q;
  wire [31:24] barrelshifter_2_out_2;

  Counter #(.Bits(32)) counter_1 (.en(~FlushD), .C(CLK), .clr(counter_1_ovf), .out(counter_1_out), .ovf(counter_1_ovf));
  BarrelShifter #(.Bits(32)) barrelshifter_1 (.in(counter_1_out), .shift(6'b000010), .out(Fetch));
  Register #(.Bits(32)) register_1 (.D(Fetch), .C(CLK), .en(1'b1), .Q(Decode));
  Register #(.Bits(32)) register_2 (.D(Decode), .C(CLK), .en(1'b1), .Q(Execute));
  Register #(.Bits(32)) register_3 (.D(Execute), .C(CLK), .en(1'b1), .Q(Memory));
  Register #(.Bits(32)) register_4 (.D(Memory), .C(CLK), .en(1'b1), .Q(WriteBack));
  Register #(.Bits(32)) register_5 (.D(WriteBack), .C(CLK), .en(1'b1));  // open: Q
  Multiplexer #(.Bits(32)) multiplexer_1 (
    .sel(PCSrcE), .in_0(_32adder_1_out), .in_1(_32adder_2_out), .out(multiplexer_1_out));
  Register #(.Bits(32), .isProgramCounter("true")) PC (
    .D(multiplexer_1_out), .C(CLK), .en(~hazard_unit_1_stallf), .Q(PC_q));
  and and_1 (and_1_out, Clock, ~Stop);  // And
  BarrelShifter #(.Bits(32), .direction("right")) barrelshifter_2 (
    .in(PC_q), .shift(6'b000010), .out({barrelshifter_2_out_2, barrelshifter_2_out}));
  or or_1 (CLK, and_1_out, Step);
  _32Adder _32adder_1 (.A(PC_q), .B(32'h4), .Out(_32adder_1_out), .C_O(_32adder_1_c_o));
  ROM #(.AddrBits(24), .Bits(32)) rom_1 (.A(barrelshifter_2_out), .sel(1'b1), .D(rom_1_d));
  // Probe on Fetch
  LED led_1 (.in(_32adder_1_c_o));
  not not_1 (not_1_out, hazard_unit_1_stalld);
  not not_2 (not_2_out, hazard_unit_1_stalld);
  not not_3 (not_3_out, hazard_unit_1_stalld);
  RegisterCLR32 InstrD (.D(rom_1_d), .CLK(CLK), .en(not_1_out), .CLR(FlushD), .Q(InstrD_q));
  RegisterCLR32 PCD (.D(PC_q), .CLK(CLK), .en(not_2_out), .CLR(FlushD), .Q(PCD_q));
  RegisterCLR32 PCPlus4D (.D(_32adder_1_out), .CLK(CLK), .en(not_3_out), .CLR(FlushD), .Q(PCPlus4D_q));
  // CU_Pipelined cu_pipelined_1: pin names not known; wires that end beside it: InstrD_q, cu_pipelined_1_p2, cu_pipelined_1_p3, cu_pipelined_1_p4, cu_pipelined_1_p5, cu_pipelined_1_p6, cu_pipelined_1_p7, cu_pipelined_1_p8, ImmSrc, cu_pipelined_1_p10
  not not_4 (not_4_out, CLK);
  RegisterFile #(.AddrBits(5), .Bits(32)) Register_File (
    .Din(multiplexer_5_out), .we(RegWriteW), .Rw(RdW_q), .C(not_4_out), .Ra(InstrD_q[19:15]),
    .Rb(InstrD_q[24:20]), .Da(Register_File_da), .Db(Register_File_db));
  Hazard_Unit hazard_unit_1 (
    .Rs1D(InstrD_q[19:15]), .Rs2D(InstrD_q[24:20]), .Rs2E(Rs2E_q), .Rs1E(Rs1E_q), .RdE(RdE_q),
    .PCSrcE(PCSrcE), .ResultSrcE(ResultSrcE_q), .RdM(RdM_q), .RegWriteM(RegWriteM_q), .RdW(RdW_q),
    .RegWriteW(RegWriteW), .StallF(hazard_unit_1_stallf), .StallD(hazard_unit_1_stalld), .FlushD(FlushD),
    .FlushE(FlushE), .ForwardAE(hazard_unit_1_forwardae), .ForwardBE(hazard_unit_1_forwardbe));
  // Probe on ImmSrc
  sign_Extension sign_extension_1 (.Input(InstrD_q[31:7]), .ImmSrc(ImmSrc), .ImmExt(sign_extension_1_immext));
  // Probe on Decode
  // RegisterCLR3 ALUControlE: pin names not known; wires that end beside it: cu_pipelined_1_p10, CLK, 1'b1, FlushE, ALUControlE_p5
  RegisterCLR RegWriteE (.D(cu_pipelined_1_p2), .CLK(CLK), .en(1'b1), .CLR(FlushE), .Q(RegWriteE_q));
  RegisterCLR2 ResultSrcE (.D(cu_pipelined_1_p3), .CLK(CLK), .en(1'b1), .CLR(FlushE), .Q(ResultSrcE_q));
  RegisterCLR MemWriteE (.D(cu_pipelined_1_p4), .CLK(CLK), .en(1'b1), .CLR(FlushE), .Q(MemWriteE_q));
  RegisterCLR JumpE (.D(cu_pipelined_1_p5), .CLK(CLK), .en(1'b1), .CLR(FlushE), .Q(JumpE_q));
  RegisterCLR BranchE (.D(cu_pipelined_1_p6), .CLK(CLK), .en(1'b1), .CLR(FlushE), .Q(BranchE_q));
  RegisterCLR3 ALUControlE_2 (.D(cu_pipelined_1_p7), .CLK(CLK), .en(1'b1), .CLR(FlushE), .Q(ALUControl));
  RegisterCLR ALUSrcE (.D(cu_pipelined_1_p8), .CLK(CLK), .en(1'b1), .CLR(FlushE), .Q(ALUSrcE_q));
  RegisterCLR32 RD1E (.D(Register_File_da), .CLK(CLK), .en(1'b1), .CLR(FlushE), .Q(RD1E_q));
  RegisterCLR32 RE2E (.D(Register_File_db), .CLK(CLK), .en(1'b1), .CLR(FlushE), .Q(RE2E_q));
  RegisterCLR32 ImmExtE (.D(sign_extension_1_immext), .CLK(CLK), .en(1'b1), .CLR(FlushE), .Q(ImmExtE_q));
  RegisterCLR5 RdE (.D(InstrD_q[11:7]), .CLK(CLK), .en(1'b1), .CLR(FlushE), .Q(RdE_q));
  RegisterCLR32 PCE (.D(PCD_q), .CLK(CLK), .en(1'b1), .CLR(FlushE), .Q(PCE_q));
  RegisterCLR32 PCPlus4E (.D(PCPlus4D_q), .CLK(CLK), .en(1'b1), .CLR(FlushE), .Q(PCPlus4E_q));
  RegisterCLR5 Rs1E (.D(InstrD_q[19:15]), .CLK(CLK), .en(1'b1), .CLR(FlushE), .Q(Rs1E_q));
  RegisterCLR5 Rs2E (.D(InstrD_q[24:20]), .CLK(CLK), .en(1'b1), .CLR(FlushE), .Q(Rs2E_q));
  Multiplexer #(.Selector_Bits(2), .Bits(32)) multiplexer_2 (
    .sel(hazard_unit_1_forwardae), .in_0(RD1E_q), .in_1(multiplexer_5_out), .in_2(ALUResultM_q),
    .in_3({32{1'b0}}), .out(multiplexer_2_out));
  // BranchConditions branchconditions_1: pin names not known; wires that end beside it: ALUControlE_p5, BranchE_q, branchconditions_1_p3, branchconditions_1_p4
  Multiplexer #(.Selector_Bits(2), .Bits(32)) multiplexer_3 (
    .sel(hazard_unit_1_forwardbe), .in_0(RE2E_q), .in_1(multiplexer_5_out), .in_2(ALUResultM_q),
    .in_3({32{1'b0}}), .out(multiplexer_3_out));
  Multiplexer #(.Bits(32)) multiplexer_4 (
    .sel(ALUSrcE_q), .in_0(multiplexer_3_out), .in_1(ImmExtE_q), .out(multiplexer_4_out));
  _32Adder _32adder_2 (.A(ImmExtE_q), .B(PCE_q), .Out(_32adder_2_out), .C_O(_32adder_2_c_o));
  // Probe on ALUControl
  // ALU alu_1: pin names not known; wires that end beside it: ALUControl, multiplexer_2_out, multiplexer_4_out, alu_1_p4, branchconditions_1_p3
  // Probe on multiplexer_4_out
  LED led_2 (.in(_32adder_2_c_o));
  or or_2 (PCSrcE, JumpE_q, branchconditions_1_p4);
  // Probe on Execute
  Register RegWriteM (.D(RegWriteE_q), .C(CLK), .en(1'b1), .Q(RegWriteM_q));
  Register #(.Bits(2)) ResultSrcM (.D(ResultSrcE_q), .C(CLK), .en(1'b1), .Q(ResultSrcM_q));
  Register MemWriteM (.D(MemWriteE_q), .C(CLK), .en(1'b1), .Q(MemWrite));
  Register #(.Bits(32)) ALUResultM (.D(alu_1_p4), .C(CLK), .en(1'b1), .Q(ALUResultM_q));
  Register #(.Bits(32)) WriteDataM (.D(multiplexer_3_out), .C(CLK), .en(1'b1), .Q(WriteDataM_q));
  Register #(.Bits(5)) RdM (.D(RdE_q), .C(CLK), .en(1'b1), .Q(RdM_q));
  Register #(.Bits(32)) PCPlus4M (.D(PCPlus4E_q), .C(CLK), .en(1'b1), .Q(PCPlus4M_q));
  ROM #(.AddrBits(24), .Bits(32)) rom_2 (.A(24'h1), .sel(1'b0), .D(out_2));
  myRAM myram_1 (
    .A(ALUResultM_q), .Din(WriteDataM_q), .str(MemWrite), .C(CLK), .ld(1'b1), .StoreWHB(2'b00), .D(myram_1_d));
  RAMDualPort #(.AddrBits(24), .isProgramMemory("true"), .Bits(32)) ramdualport_1 (
    .A(ALUResultM_q[23:0]), .Din(WriteDataM_q), .str(MemWrite), .C(CLK), .ld(1'b1), .D(ramdualport_1_d));
  // Probe on Memory
  // Probe on myram_1_d
  Register u_RegWriteW (.D(RegWriteM_q), .C(CLK), .en(1'b1), .Q(RegWriteW));
  Register #(.Bits(2)) ResultSrcW (.D(ResultSrcM_q), .C(CLK), .en(1'b1), .Q(ResultSrcW_q));
  Register #(.Bits(32)) ALUResultW (.D(ALUResultM_q), .C(CLK), .en(1'b1), .Q(ALUResultW_q));
  Register #(.Bits(32)) ReadDataW (.D(ramdualport_1_d), .C(CLK), .en(1'b1), .Q(ReadDataW_q));
  Register #(.Bits(5)) RdW (.D(RdM_q), .C(CLK), .en(1'b1), .Q(RdW_q));
  Register #(.Bits(32)) PCPlus4W (.D(PCPlus4M_q), .C(CLK), .en(1'b1), .Q(PCPlus4W_q));
  // Probe on WriteBack
  Multiplexer #(.Selector_Bits(2), .Bits(32)) multiplexer_5 (
    .sel(ResultSrcW_q), .in_0(ALUResultW_q), .in_1(ReadDataW_q), .in_2(PCPlus4W_q), .in_3({32{1'b0}}),
    .out(multiplexer_5_out));

  // Notes on the sheet:
  //   Clock: Hz: 5
  //   Fetch
  //   Hazard Unit
  //   Cycle Decode
  //   contents of rom_1 (hex, n*v repeats v):
  //   ffc4a303,64a423,62e233,fe420ae3
  //   Flush Registers
  //   Decode
  //   FE420AE3
  //   Execute
  //   Memory
  //   contents of rom_2 (hex, n*v repeats v):
  //   1,0,1,1
  //   Writeback
  //   Cycle WriteBack
endmodule
