// Digital circuit RegisterCLR3.dig as structural Verilog
module RegisterCLR3 (
  input  [2:0] D,
  input  CLK,
  input  en,
  input  CLR,
  output [2:0] Q
);

  wire or_1_out;
  wire [2:0] multiplexer_1_out;

  Multiplexer #(.Bits(3)) multiplexer_1 (.sel(CLR), .in_0(D), .in_1(3'b000), .out(multiplexer_1_out));
  or or_1 (or_1_out, en, CLR);
  Register #(.Bits(3)) register_1 (.D(multiplexer_1_out), .C(CLK), .en(or_1_out), .Q(Q));
endmodule
