// Digital circuit RegisterCLR5.dig as structural Verilog
module RegisterCLR5 (
  input  [4:0] D,
  input  CLK,
  input  en,
  input  CLR,
  output [4:0] Q
);

  wire or_1_out;
  wire [4:0] multiplexer_1_out;

  Multiplexer #(.Bits(5)) multiplexer_1 (.sel(CLR), .in_0(D), .in_1({5{1'b0}}), .out(multiplexer_1_out));
  or or_1 (or_1_out, en, CLR);
  Register #(.Bits(5)) register_1 (.D(multiplexer_1_out), .C(CLK), .en(or_1_out), .Q(Q));
endmodule
