// Digital circuit SingleCycleProcessor.dig as structural Verilog
module SingleCycleProcessor (
  input  clk
);

  wire and_1_out, cu_singlecycle_1_alusrc, cu_singlecycle_1_branch, cu_singlecycle_1_jump,
       cu_singlecycle_1_memwrite, cu_singlecycle_1_regwrite, or_1_out, reset_1_out;
  wire [1:0] cu_singlecycle_1_immsrc, cu_singlecycle_1_resultsrc;
  wire [2:0] cu_singlecycle_1_alucontrol;
  wire [3:0] new_alu_1_nzcv_flags;
  wire [4:0] ROM_d_2, ROM_d_3;
  wire [23:0] new_alu_1_out;
  wire [31:0] add_1_s, add_2_s, barrelshifter_1_out, multiplexer_1_out, multiplexer_2_out, multiplexer_3_out,
       PC_q, ramdualport_1_d, registerfile_1_da, registerfile_1_db, ROM_d, sign_extension_1_immext;
  wire [31:24] new_alu_1_out_2;

  Reset reset_1 (.out(reset_1_out));
  Register #(.Bits(32), .isProgramCounter("true")) PC (.D(multiplexer_2_out), .C(clk), .en(reset_1_out), .Q(PC_q));
  // Probe on PC_q
  BarrelShifter #(.Bits(32), .barrelShifterMode("arithmetic"), .direction("right")) barrelshifter_1 (
    .in(PC_q), .shift(6'b000010), .out(barrelshifter_1_out));
  // Probe on barrelshifter_1_out
  Add #(.Bits(32)) add_1 (.a(PC_q), .b(32'h4), .c_i(1'b0), .s(add_1_s));  // open: c_o
  ROM #(.AddrBits(24), .Bits(32)) ROM (
    .A(barrelshifter_1_out[23:0]), .sel(1'b1), .D({ROM_d[31:25], ROM_d_3, ROM_d[19:12], ROM_d_2, ROM_d[6:0]}));
  // Probe on {ROM_d[31:25], ROM_d_3, ROM_d[19:12], ROM_d_2, ROM_d[6:0]}
  CU_Singlecycle cu_singlecycle_1 (
    .Instruction({ROM_d[31:25], ROM_d_3, ROM_d[19:12], ROM_d_2, ROM_d[6:0]}),
    .RegWrite(cu_singlecycle_1_regwrite), .ALUSrc(cu_singlecycle_1_alusrc),
    .MemWrite(cu_singlecycle_1_memwrite), .Branch(cu_singlecycle_1_branch), .Jump(cu_singlecycle_1_jump),
    .ResultSrc(cu_singlecycle_1_resultsrc), .ImmSrc(cu_singlecycle_1_immsrc),
    .ALUControl(cu_singlecycle_1_alucontrol));
  sign_Extension sign_extension_1 (
    .Input({ROM_d[31:25], ROM_d_3, ROM_d[19:12], ROM_d_2}), .ImmSrc(cu_singlecycle_1_immsrc),
    .ImmExt(sign_extension_1_immext));
  RegisterFile #(.AddrBits(5), .Bits(32)) registerfile_1 (
    .Din(multiplexer_3_out), .we(cu_singlecycle_1_regwrite), .Rw(ROM_d_2), .C(clk), .Ra(ROM_d[19:15]),
    .Rb(ROM_d_3), .Da(registerfile_1_da), .Db(registerfile_1_db));
  Multiplexer #(.Bits(32)) multiplexer_1 (
    .sel(cu_singlecycle_1_alusrc), .in_0(registerfile_1_db), .in_1(sign_extension_1_immext),
    .out(multiplexer_1_out));
  Add #(.Bits(32)) add_2 (.a(PC_q), .b(sign_extension_1_immext), .c_i(1'b0), .s(add_2_s));  // open: c_o
  new_ALU new_alu_1 (
    .ALUControl(cu_singlecycle_1_alucontrol), .A(registerfile_1_da), .B(multiplexer_1_out),
    .OUT({new_alu_1_out_2, new_alu_1_out}), .NZCV_Flags(new_alu_1_nzcv_flags));
  Multiplexer #(.Bits(32)) multiplexer_2 (.sel(or_1_out), .in_0(add_1_s), .in_1(add_2_s), .out(multiplexer_2_out));
  or or_1 (or_1_out, and_1_out, cu_singlecycle_1_jump);
  and and_1 (and_1_out, new_alu_1_nzcv_flags[1], cu_singlecycle_1_branch);
  RAMDualPort #(.AddrBits(24), .isProgramMemory("true"), .Bits(32)) ramdualport_1 (
    .A(new_alu_1_out), .Din(registerfile_1_db), .str(cu_singlecycle_1_memwrite), .C(clk), .ld(1'b1),
    .D(ramdualport_1_d));
  Multiplexer #(.Selector_Bits(2), .Bits(32)) multiplexer_3 (
    .sel(cu_singlecycle_1_resultsrc), .in_0({new_alu_1_out_2, new_alu_1_out}), .in_1(ramdualport_1_d),
    .in_2({32{1'b0}}), .in_3({32{1'b0}}), .out(multiplexer_3_out));

  // Notes on the sheet:
  //   ROM loads test.hex
endmodule
