// Digital circuit _32Adder.dig as structural Verilog
module _32Adder (
  input  [31:0] A,
  input  [31:0] B,
  output [31:0] Out,
  output C_O
);

  wire _8_full_adder_1_c_arry, _8_full_adder_2_c_arry, _8_full_adder_3_c_arry;

  _8_full_adder _8_full_adder_1 (
    .Y(Out[7:0]), .C_arry(_8_full_adder_1_c_arry), .A(A[7:0]), .B(B[7:0]), .subtract(1'b0), .Carry_in(1'b0));
  _8_full_adder _8_full_adder_2 (
    .Y(Out[15:8]), .C_arry(_8_full_adder_2_c_arry), .A(A[15:8]), .B(B[15:8]), .subtract(1'b0),
    .Carry_in(_8_full_adder_1_c_arry));
  _8_full_adder _8_full_adder_3 (
    .Y(Out[23:16]), .C_arry(_8_full_adder_3_c_arry), .A(A[23:16]), .B(B[23:16]), .subtract(1'b0),
    .Carry_in(_8_full_adder_2_c_arry));
  _8_full_adder _8_full_adder_4 (
    .Y(Out[31:24]), .C_arry(C_O), .A(A[31:24]), .B(B[31:24]), .subtract(1'b0),
    .Carry_in(_8_full_adder_3_c_arry));
endmodule
