// Digital circuit _full_adder.dig as structural Verilog
module full_adder (
  input  Carry_in,
  input  A,
  input  B,
  output Carry_out,
  output Y
);

  wire and_1_out, and_2_out, xor_1_out;

  xor xor_1 (xor_1_out, A, B);
  and and_1 (and_1_out, A, B);
  xor xor_2 (Y, xor_1_out, Carry_in);
  and and_2 (and_2_out, xor_1_out, Carry_in);
  or or_1 (Carry_out, and_1_out, and_2_out);
endmodule

/* Test case:
A B Carry_in Y Carry_out

0 0 0 0 0
0 1 0 1 0
1 0 0 1 0
1 1 0 0 1
0 0 1 1 0
0 1 1 0 1
1 0 1 0 1
1 1 1 1 1
*/
