// Digital circuit _instruction_decoder.dig as structural Verilog
module instruction_decoder (
  input  [31:0] Instruction,
  input  Zero,
  input  CLK,
  output [1:0] ALUSrcA,
  output [1:0] ALUSrcB,
  output [1:0] ResultSrc,
  output [2:0] ALUControl,
  output PCWrite,
  output [1:0] ImmSrc,
  output AdrSrc,
  output IRWrite,
  output MemWrite,
  output RegWrite
);

  wire and_1_out, and_2_out, and_3_out, and_4_out, and_5_out, and_6_out, and_7_out, and_8_out, and_9_out,
       and_10_out, and_11_out, and_12_out, and_13_out, and_14_out, and_15_out, and_16_out, and_17_out,
       and_18_out, and_19_out, and_20_out, and_21_out, and_22_out, and_23_out, and_24_out, and_25_out,
       and_26_out, and_27_out, and_28_out, and_29_out, and_30_out, and_31_out, and_32_out, and_33_out,
       and_34_out, and_35_out, and_36_out, and_37_out, and_38_out, and_39_out, and_40_out, and_41_out,
       and_42_out, and_43_out, and_44_out, and_45_out, and_46_out, and_47_out, and_48_out, and_49_out,
       and_50_out, and_51_out, and_52_out, and_53_out, and_54_out, and_55_out, and_56_out, and_57_out,
       and_58_out, and_59_out, and_60_out, and_61_out, and_62_out, and_63_out, and_64_out, and_65_out,
       and_66_out, and_67_out, and_68_out, and_69_out, and_71_out, and_72_out, and_73_out, and_74_out,
       and_75_out, and_76_out, and_77_out, and_78_out, and_79_out, and_80_out, and_81_out, and_82_out,
       and_83_out, and_84_out, and_86_out, and_88_out, and_89_out, and_90_out, and_91_out, and_92_out,
       and_93_out, and_94_out, and_95_out, and_96_out, and_97_out, and_98_out, and_99_out, and_100_out,
       and_101_out, and_102_out, and_103_out, and_104_out, and_105_out, and_106_out, and_107_out,
       and_108_out, and_109_out, and_110_out, and_111_out, and_112_out, and_113_out, and_114_out,
       and_115_out, and_116_out, and_117_out, and_118_out, and_119_out, and_120_out, and_121_out,
       and_123_out, and_124_out, and_125_out, and_126_out, and_127_out, and_129_out, and_130_out,
       and_131_out, and_134_out, and_135_out, and_136_out, and_137_out, and_138_out, and_139_out,
       and_140_out, and_141_out, and_142_out, and_143_out, Branch, not_1_out, not_2_out, not_3_out,
       not_4_out, not_5_out, not_6_out, not_7_out, not_8_out, not_9_out, not_10_out, not_11_out, not_12_out,
       not_13_out, not_14_out, not_15_out, not_16_out, not_17_out, not_18_out, not_19_out, or_2_out,
       or_3_out, or_4_out, or_5_out, or_7_out, or_12_out, or_13_out, or_14_out, or_15_out, or_16_out,
       or_18_out, or_23_out, or_24_out, or_25_out, or_26_out, or_27_out, or_29_out, or_30_out, or_31_out,
       or_32_out, or_33_out, or_34_out, or_35_out, PCUpdate, priorityencoder_1_any, Z_0_n, Z_1_n, Z_2_n,
       Z_3_n;
  wire [1:0] ALUOp;
  wire [2:0] ALU, F_type;
  wire [24:0] demultiplexer_1_out_6, demultiplexer_1_out_7, Type_B, Type_I, Type_J, Type_R, Type_S, Type_U;

  not not_1 (not_1_out, Instruction[14]);
  not not_2 (not_2_out, Instruction[2]);
  not not_3 (not_3_out, Instruction[13]);
  not not_4 (not_4_out, Instruction[12]);
  not not_5 (not_5_out, Instruction[3]);
  and and_1 (and_1_out, Zero, Branch);
  not not_6 (not_6_out, Instruction[5]);
  not not_7 (not_7_out, Instruction[4]);
  not not_8 (not_8_out, Instruction[30]);
  and and_2 (and_2_out, Instruction[12], not_1_out);
  and and_3 (and_3_out, not_4_out, not_3_out);
  and and_4 (and_4_out, Instruction[13], not_1_out);
  and and_5 (and_5_out, Instruction[12], not_3_out);
  and and_6 (and_6_out, not_4_out, Instruction[14]);
  and and_7 (and_7_out, Instruction[13], Instruction[14]);
  and and_8 (and_8_out, not_4_out, not_1_out);
  and and_9 (and_9_out, Instruction[30], Instruction[5]);
  and and_10 (and_10_out, not_4_out, Instruction[14]);
  and and_11 (and_11_out, not_4_out, Instruction[14]);
  and and_12 (and_12_out, not_4_out, Instruction[13]);
  not not_9 (not_9_out, Instruction[5]);
  not not_10 (not_10_out, Instruction[6]);
  or or_1 (PCWrite, and_1_out, PCUpdate);
  and and_13 (and_13_out, Instruction[5], not_10_out);
  and and_14 (and_14_out, Instruction[4], Instruction[2]);
  and and_15 (and_15_out, Instruction[6], not_2_out);
  and and_16 (and_16_out, Instruction[4], not_2_out);
  and and_17 (and_17_out, Instruction[5], not_7_out);
  and and_18 (and_18_out, not_9_out, not_2_out);
  and and_19 (and_19_out, not_5_out, Instruction[2]);
  and and_20 (and_20_out, and_3_out, Instruction[14]);
  and and_21 (and_21_out, and_5_out, not_1_out);
  and and_22 (and_22_out, and_8_out, and_9_out);
  and and_23 (and_23_out, and_10_out, not_8_out);
  and and_24 (and_24_out, and_11_out, not_6_out);
  and and_25 (and_25_out, and_16_out, Instruction[5]);
  and and_26 (and_26_out, and_17_out, not_10_out);
  and and_27 (and_27_out, and_19_out, not_10_out);
  or or_2 (or_2_out, and_2_out, and_20_out);
  or or_3 (or_3_out, and_21_out, and_6_out);
  or or_4 (or_4_out, and_22_out, and_23_out);
  or or_5 (or_5_out, and_24_out, and_12_out);
  Multiplexer #(.Selector_Bits(2), .Bits(3)) multiplexer_1 (
    .sel(ALUOp), .in_0(3'b000), .in_1(3'b001), .in_2(ALU), .in_3(3'b111), .out(ALUControl));
  or or_6 (ImmSrc[0], Instruction[2], and_13_out);
  or or_7 (or_7_out, and_18_out, and_27_out);
  or or_8 (ALU[2], or_2_out, and_4_out);
  or or_9 (ALU[1], or_3_out, and_7_out);
  or or_10 (ALU[0], or_4_out, or_5_out);
  Demultiplexer #(.Selector_Bits(3), .Bits(25)) demultiplexer_1 (
    .sel(F_type), .in(Instruction[31:7]), .out_0(Type_U), .out_1(Type_J), .out_2(Type_B), .out_3(Type_R),
    .out_4(Type_S), .out_5(Type_I), .out_6(demultiplexer_1_out_6), .out_7(demultiplexer_1_out_7));
  // Probe Multicycle_CU.fsm on {Z_3_n, Z_2_n, Z_1_n, Z_0_n}
  PriorityEncoder #(.Selector_Bits(3)) priorityencoder_1 (
    .in0(and_14_out), .in1(Instruction[3]), .in2(and_15_out), .in3(and_25_out), .in4(and_26_out),
    .in5(or_7_out), .in6(1'b0), .in7(1'b0), .num(F_type), .any(priorityencoder_1_any));
  LED led_1 (.in(priorityencoder_1_any));
  not not_11 (not_11_out, Instruction[2]);
  not not_12 (not_12_out, Instruction[3]);
  not not_13 (not_13_out, Instruction[4]);
  not not_14 (not_14_out, Instruction[5]);
  not not_15 (not_15_out, Instruction[6]);
  not not_16 (not_16_out, Z_3_n);
  not not_17 (not_17_out, Z_2_n);
  not not_18 (not_18_out, Z_1_n);
  not not_19 (not_19_out, Z_0_n);
  and and_28 (and_28_out, Z_0_n, not_18_out);
  and and_29 (and_29_out, not_16_out, not_11_out);
  and and_30 (and_30_out, not_12_out, not_13_out);
  and and_31 (and_31_out, Instruction[5], Instruction[6]);
  and and_32 (and_32_out, Z_0_n, not_18_out);
  and and_33 (and_33_out, not_16_out, not_11_out);
  and and_34 (and_34_out, not_12_out, Instruction[4]);
  and and_35 (and_35_out, not_14_out, not_15_out);
  and and_36 (and_36_out, Z_0_n, not_18_out);
  and and_37 (and_37_out, not_16_out, Instruction[2]);
  and and_38 (and_38_out, Instruction[3], not_13_out);
  and and_39 (and_39_out, Instruction[5], Instruction[6]);
  and and_40 (and_40_out, Z_0_n, not_17_out);
  and and_41 (and_41_out, not_11_out, not_12_out);
  and and_42 (and_42_out, Instruction[4], Instruction[5]);
  and and_43 (and_43_out, not_19_out, Z_1_n);
  and and_44 (and_44_out, not_16_out, Instruction[5]);
  and and_45 (and_45_out, Z_0_n, Z_1_n);
  and and_46 (and_46_out, not_19_out, Z_1_n);
  and and_47 (and_47_out, not_18_out, Z_3_n);
  and and_48 (and_48_out, Z_0_n, not_18_out);
  and and_49 (and_49_out, not_17_out, not_11_out);
  and and_50 (and_50_out, not_12_out, Instruction[5]);
  and and_51 (and_51_out, Z_0_n, not_18_out);
  and and_52 (and_52_out, not_17_out, not_11_out);
  and and_53 (and_53_out, not_12_out, not_13_out);
  and and_54 (and_54_out, Z_0_n, not_18_out);
  and and_55 (and_55_out, not_17_out, not_11_out);
  and and_56 (and_56_out, not_12_out, not_13_out);
  and and_57 (and_57_out, not_19_out, Z_1_n);
  and and_58 (and_58_out, not_16_out, not_14_out);
  and and_59 (and_59_out, not_19_out, Z_1_n);
  and and_60 (and_60_out, not_18_out, Z_3_n);
  and and_61 (and_61_out, not_19_out, not_18_out);
  and and_62 (and_62_out, not_19_out, Z_1_n);
  and and_63 (and_63_out, not_18_out, not_17_out);
  and and_64 (and_64_out, not_14_out, Instruction[6]);
  and and_65 (and_65_out, not_18_out, not_17_out);
  and and_66 (and_66_out, Instruction[4], Instruction[6]);
  and and_67 (and_67_out, not_18_out, not_17_out);
  and and_68 (and_68_out, not_18_out, not_17_out);
  and and_69 (and_69_out, not_18_out, Z_3_n);
  and and_70 (ALUOp[0], Z_1_n, Z_3_n);
  and and_71 (and_71_out, not_19_out, Z_2_n);
  and and_72 (and_72_out, not_19_out, not_18_out);
  and and_73 (and_73_out, Z_0_n, not_18_out);
  and and_74 (and_74_out, not_19_out, Z_1_n);
  and and_75 (and_75_out, not_19_out, Z_3_n);
  and and_76 (and_76_out, Z_0_n, not_18_out);
  and and_77 (and_77_out, not_17_out, not_16_out);
  and and_78 (and_78_out, not_19_out, Z_1_n);
  and and_79 (and_79_out, not_17_out, not_16_out);
  and and_80 (and_80_out, not_19_out, not_18_out);
  and and_81 (and_81_out, not_19_out, not_18_out);
  and and_82 (and_82_out, Z_0_n, Z_3_n);
  and and_83 (and_83_out, Z_0_n, Z_1_n);
  and and_84 (and_84_out, not_18_out, Z_2_n);
  and and_85 (Branch, Z_1_n, Z_3_n);
  and and_86 (and_86_out, not_19_out, not_18_out);
  and and_87 (MemWrite, not_18_out, Z_2_n);
  and and_88 (and_88_out, not_19_out, not_18_out);
  and and_89 (and_89_out, not_17_out, not_16_out);
  and and_90 (and_90_out, Z_0_n, Z_3_n);
  and and_91 (and_91_out, not_19_out, not_18_out);
  and and_92 (and_92_out, Z_0_n, Z_1_n);
  and and_93 (and_93_out, not_19_out, not_18_out);
  and and_94 (and_94_out, not_19_out, not_18_out);
  and and_95 (and_95_out, not_17_out, not_16_out);
  and and_96 (and_96_out, and_28_out, not_17_out);
  and and_97 (and_97_out, and_30_out, and_31_out);
  and and_98 (and_98_out, and_32_out, not_17_out);
  and and_99 (and_99_out, and_34_out, and_35_out);
  and and_100 (and_100_out, and_36_out, not_17_out);
  and and_101 (and_101_out, and_38_out, and_39_out);
  and and_102 (and_102_out, and_40_out, and_41_out);
  and and_103 (and_103_out, and_42_out, not_15_out);
  and and_104 (and_104_out, and_43_out, and_44_out);
  and and_105 (and_105_out, and_45_out, not_17_out);
  and and_106 (and_106_out, and_46_out, Z_2_n);
  and and_107 (and_107_out, and_48_out, and_49_out);
  and and_108 (and_108_out, and_50_out, not_15_out);
  and and_109 (and_109_out, and_51_out, and_52_out);
  and and_110 (and_110_out, and_53_out, not_15_out);
  and and_111 (and_111_out, and_54_out, and_55_out);
  and and_112 (and_112_out, and_56_out, Instruction[5]);
  and and_113 (and_113_out, and_57_out, and_58_out);
  and and_114 (and_114_out, and_59_out, Z_2_n);
  and and_115 (and_115_out, and_61_out, not_17_out);
  and and_116 (and_116_out, and_62_out, not_16_out);
  and and_117 (and_117_out, and_63_out, and_64_out);
  and and_118 (and_118_out, and_65_out, and_66_out);
  and and_119 (and_119_out, and_67_out, Instruction[3]);
  and and_120 (and_120_out, and_68_out, Instruction[2]);
  and and_121 (and_121_out, and_72_out, Z_3_n);
  and and_122 (ALUSrcA[0], and_73_out, not_17_out);
  or or_11 (ALUSrcA[1], and_74_out, and_75_out);
  and and_123 (and_123_out, and_76_out, and_77_out);
  and and_124 (and_124_out, and_78_out, and_79_out);
  and and_125 (and_125_out, and_80_out, Z_3_n);
  and and_126 (and_126_out, and_81_out, not_16_out);
  and and_127 (and_127_out, and_83_out, not_17_out);
  and and_128 (IRWrite, and_86_out, not_16_out);
  and and_129 (and_129_out, and_88_out, and_89_out);
  and and_130 (and_130_out, and_91_out, Z_2_n);
  and and_131 (and_131_out, and_92_out, Z_2_n);
  and and_132 (ResultSrc[0], and_93_out, Z_2_n);
  and and_133 (ResultSrc[1], and_94_out, and_95_out);
  and and_134 (and_134_out, and_96_out, and_29_out);
  and and_135 (and_135_out, and_98_out, and_33_out);
  and and_136 (and_136_out, and_100_out, and_37_out);
  and and_137 (and_137_out, and_102_out, and_103_out);
  or or_12 (or_12_out, and_106_out, and_47_out);
  and and_138 (and_138_out, and_107_out, and_108_out);
  and and_139 (and_139_out, and_109_out, and_110_out);
  and and_140 (and_140_out, and_111_out, and_112_out);
  or or_13 (or_13_out, and_113_out, and_114_out);
  or or_14 (or_14_out, and_115_out, and_116_out);
  or or_15 (or_15_out, and_117_out, and_118_out);
  or or_16 (or_16_out, and_119_out, and_120_out);
  or or_17 (ALUOp[1], and_71_out, and_121_out);
  or or_18 (or_18_out, and_123_out, and_124_out);
  or or_19 (ALUSrcB[1], and_126_out, and_82_out);
  or or_20 (AdrSrc, and_127_out, and_84_out);
  or or_21 (PCUpdate, and_129_out, and_90_out);
  or or_22 (RegWrite, and_130_out, and_131_out);
  and and_141 (and_141_out, and_134_out, and_97_out);
  and and_142 (and_142_out, and_135_out, and_99_out);
  and and_143 (and_143_out, and_136_out, and_101_out);
  or or_23 (or_23_out, and_137_out, and_104_out);
  or or_24 (or_24_out, and_138_out, and_139_out);
  or or_25 (or_25_out, or_13_out, and_60_out);
  or or_26 (or_26_out, or_14_out, or_15_out);
  or or_27 (or_27_out, or_16_out, and_69_out);
  or or_28 (ALUSrcB[0], or_18_out, and_125_out);
  or or_29 (or_29_out, and_141_out, and_142_out);
  or or_30 (or_30_out, or_23_out, and_105_out);
  or or_31 (or_31_out, or_24_out, and_140_out);
  or or_32 (or_32_out, or_26_out, or_27_out);
  or or_33 (or_33_out, or_29_out, and_143_out);
  or or_34 (or_34_out, or_30_out, or_12_out);
  or or_35 (or_35_out, or_31_out, or_25_out);
  D_FF u_Z_3_n (.D(or_33_out), .C(CLK), .Q(Z_3_n));  // open: nQ
  D_FF u_Z_2_n (.D(or_34_out), .C(CLK), .Q(Z_2_n));  // open: nQ
  D_FF u_Z_1_n (.D(or_35_out), .C(CLK), .Q(Z_1_n));  // open: nQ
  D_FF u_Z_0_n (.D(or_32_out), .C(CLK), .Q(Z_0_n));  // open: nQ

  assign ImmSrc[1] = Instruction[6];

  // Other names for the same wires on the sheet: ALUControl_0 = ALU[0]; ALUControl_1 = ALU[1]; ALUControl_2 = ALU[2];
  //   ImmSrc_0 = ImmSrc[0]; op_0 = Instruction[0]; op_1 = Instruction[1]; op_2 = Instruction[2];
  //   op_3 = Instruction[3]; op_4 = Instruction[4]; op_5 = Instruction[5]; ImmSrc_1 = Instruction[6];
  //   op_6 = Instruction[6]; func3_0 = Instruction[12]; func3_1 = Instruction[13]; func3_2 = Instruction[14];
  //   func7_5 = Instruction[30]

  // Notes on the sheet:
  //   Instruction: default 100671747
  //   ALU Decoder
  //   0x1ACCC33
  //   U
  //   J
  //   B
  //   R
  //   S
  //   I
  //   U = 000
  //   J = 001
  //   B = 010
  //   R = 011
  //   S = 100
  //   I = 101
endmodule
