// Digital circuit _sign_Extension.dig as structural Verilog
module sign_Extension (
  input  [24:0] Input,
  input  [1:0] ImmSrc,
  output [31:0] ImmExt
);

  wire [4:0] demultiplexer_1_out_3;
  wire [11:0] demultiplexer_1_out_1;
  wire [12:1] demultiplexer_1_out_2;
  wire [17:5] demultiplexer_1_out_1_2, demultiplexer_1_out_2_2;
  wire [20:1] demultiplexer_1_out_3_2;
  wire [24:0] demultiplexer_1_out_0;
  wire [31:0] bitextender_1_out, bitextender_2_out, bitextender_3_out, bitextender_4_out;

  Demultiplexer #(.Selector_Bits(2), .Bits(25)) demultiplexer_1 (
    .sel(ImmSrc), .in(Input), .out_0(demultiplexer_1_out_0),
    .out_1({demultiplexer_1_out_1[11:5], demultiplexer_1_out_1_2, demultiplexer_1_out_1[4:0]}),
    .out_2({demultiplexer_1_out_2[12], demultiplexer_1_out_2[10:5], demultiplexer_1_out_2_2, demultiplexer_1_out_2[4:1], demultiplexer_1_out_2[11]}),
    .out_3({demultiplexer_1_out_3_2[20], demultiplexer_1_out_3_2[10:1], demultiplexer_1_out_3_2[11], demultiplexer_1_out_3_2[19:12], demultiplexer_1_out_3}));
  BitExtender #(.inputBits(12), .outputBits(32)) bitextender_1 (
    .in(demultiplexer_1_out_0[24:13]), .out(bitextender_1_out));
  BitExtender #(.inputBits(12), .outputBits(32)) bitextender_2 (.in(demultiplexer_1_out_1), .out(bitextender_2_out));
  BitExtender #(.inputBits(13), .outputBits(32)) bitextender_3 (
    .in({demultiplexer_1_out_2, 1'b0}), .out(bitextender_3_out));
  BitExtender #(.inputBits(21), .outputBits(32)) bitextender_4 (
    .in({demultiplexer_1_out_3_2, 1'b0}), .out(bitextender_4_out));
  Multiplexer #(.Selector_Bits(2), .Bits(32)) multiplexer_1 (
    .sel(ImmSrc), .in_0(bitextender_1_out), .in_1(bitextender_2_out), .in_2(bitextender_3_out),
    .in_3(bitextender_4_out), .out(ImmExt));

  // Notes on the sheet:
  //   I - Type
  //   S-Type
  //   B - Type
  //   J - Type
endmodule
