// Digital circuit arith_shift.dig as structural Verilog
module arith_shift (
  input  [31:0] Input,
  input  [31:0] Shift,
  output [31:0] Y
);

  BarrelShifter #(.Bits(32), .barrelShifterMode("arithmetic"), .barrelSigned("true"), .direction("right")) Shift_Arith (
    .in(Input), .shift(Shift[6:0]), .out(Y));
endmodule

/* Test case:
Input Shift Y

loop(x,31)
	loop(s, 32)
		(1<<x) (s) ((1<<x)/1>>s)
	end loop
end loop
*/
