// Digital circuit backup_alu.dig as structural Verilog
module backup_alu (
  input  Carry_in,
  output C_arry,
  output oV_erflow,
  output Z_ero,
  output N_egative,
  output eq,
  output eq_2,
  output lt,
  output gt__eq,
  output lt__eq,
  output gt
);

  wire ALU_0, ALU_1, full_adder_1_carry_out, full_adder_2_carry_out, full_adder_3_carry_out,
       full_adder_4_carry_out, full_adder_5_carry_out, full_adder_6_carry_out, full_adder_7_carry_out,
       full_adder_8_carry_out, func7_5, multiplexer_1_out, not_1_out, xnor_1_out, xor_1_out, xor_2_out,
       xor_3_out, xor_4_out, xor_5_out, xor_6_out, xor_7_out, xor_8_out, xor_9_out;
  wire [6:0] Y;
  wire [7:0] A, B, OUT;

  Multiplexer multiplexer_1 (.sel(func7_5), .in_0(Carry_in), .in_1(func7_5), .out(multiplexer_1_out));
  xor xor_1 (xor_1_out, B[0], ALU_0);
  xor xor_2 (xor_2_out, B[1], ALU_0);
  xor xor_3 (xor_3_out, B[2], ALU_0);
  xor xor_4 (xor_4_out, B[3], ALU_0);
  xor xor_5 (xor_5_out, B[4], ALU_0);
  xor xor_6 (xor_6_out, B[5], ALU_0);
  xor xor_7 (xor_7_out, B[6], ALU_0);
  xor xor_8 (xor_8_out, B[7], ALU_0);
  full_adder full_adder_1 (
    .Carry_in(multiplexer_1_out), .Carry_out(full_adder_1_carry_out), .Y(Y[0]), .A(A[0]), .B(xor_1_out));
  full_adder full_adder_2 (
    .Carry_in(full_adder_1_carry_out), .Carry_out(full_adder_2_carry_out), .Y(Y[1]), .A(A[1]), .B(xor_2_out));
  full_adder full_adder_3 (
    .Carry_in(full_adder_2_carry_out), .Carry_out(full_adder_3_carry_out), .Y(Y[2]), .A(A[2]), .B(xor_3_out));
  full_adder full_adder_4 (
    .Carry_in(full_adder_3_carry_out), .Carry_out(full_adder_4_carry_out), .Y(Y[3]), .A(A[3]), .B(xor_4_out));
  full_adder full_adder_5 (
    .Carry_in(full_adder_4_carry_out), .Carry_out(full_adder_5_carry_out), .Y(Y[4]), .A(A[4]), .B(xor_5_out));
  full_adder full_adder_6 (
    .Carry_in(full_adder_5_carry_out), .Carry_out(full_adder_6_carry_out), .Y(Y[5]), .A(A[5]), .B(xor_6_out));
  full_adder full_adder_7 (
    .Carry_in(full_adder_6_carry_out), .Carry_out(full_adder_7_carry_out), .Y(Y[6]), .A(A[6]), .B(xor_7_out));
  full_adder full_adder_8 (
    .Carry_in(full_adder_7_carry_out), .Carry_out(full_adder_8_carry_out), .Y(N_egative), .A(A[7]),
    .B(xor_8_out));
  // Probe on {N_egative, Y}
  xnor xnor_1 (xnor_1_out, ALU_0, B[7], A[7]);
  xor xor_9 (xor_9_out, N_egative, A[7]);
  not not_1 (not_1_out, ALU_1);
  and and_1 (C_arry, not_1_out, full_adder_8_carry_out);
  and and_2 (oV_erflow, xnor_1_out, xor_9_out, not_1_out);
  nor nor_1 (eq, OUT[0], OUT[1], OUT[2], OUT[3], OUT[5], OUT[6], OUT[7], OUT[4]);
  xor xor_10 (lt, oV_erflow, N_egative);
  not not_2 (eq_2, eq);
  not not_3 (gt__eq, lt);
  or or_1 (lt__eq, lt, eq);
  not not_4 (gt, lt__eq);
  // Probe on {{7{1'b0}}, lt}

  assign Z_ero = eq;

  // Other names for the same wires on the sheet: Y[7] = N_egative; A_31 = A[7]; B_31 = B[7]; SLT[0] = lt
endmodule
