// Digital circuit myEEProm.dig as structural Verilog
module myEEProm (
  input  [31:0] A,
  input  sel,
  output [31:0] D
);

  wire [31:0] barrelshifter_1_out;

  BarrelShifter #(.Bits(32), .direction("right")) barrelshifter_1 (
    .in(A), .shift(6'b000010), .out(barrelshifter_1_out));
  ROM #(.AddrBits(24), .Bits(32)) rom_1 (.A(barrelshifter_1_out[23:0]), .sel(sel), .D(D));

  // Notes on the sheet:
  //   contents of rom_1 (hex, n*v repeats v):
  //   ffc4a303,64a423,62e233,fe420ae3
endmodule
