// Digital circuit myRAM.dig as structural Verilog
module myRAM (
  input  [31:0] A,
  input  [31:0] Din,
  input  str,
  input  C,
  input  ld,
  input  [1:0] StoreWHB,
  output [31:0] D
);

  wire multiplexer_1_out, multiplexer_2_out, multiplexer_3_out;

  Multiplexer multiplexer_1 (.sel(StoreWHB[0]), .in_0(str), .in_1(1'b0), .out(multiplexer_1_out));
  Multiplexer multiplexer_2 (.sel(StoreWHB[1]), .in_0(str), .in_1(1'b0), .out(multiplexer_2_out));
  Multiplexer multiplexer_3 (.sel(StoreWHB[1]), .in_0(str), .in_1(1'b0), .out(multiplexer_3_out));
  RAMDualPort #(.AddrBits(24), .isProgramMemory("true"), .Bits(8)) RAM_3 (
    .A(A[23:0]), .Din(Din[7:0]), .str(str), .C(C), .ld(ld), .D(D[7:0]));
  RAMDualPort #(.AddrBits(24), .isProgramMemory("true"), .Bits(8)) RAM_2 (
    .A(A[23:0]), .Din(Din[15:8]), .str(multiplexer_1_out), .C(C), .ld(ld), .D(D[15:8]));
  RAMDualPort #(.AddrBits(24), .isProgramMemory("true"), .Bits(8)) RAM_1 (
    .A(A[23:0]), .Din(Din[23:16]), .str(multiplexer_2_out), .C(C), .ld(ld), .D(D[23:16]));
  RAMDualPort #(.AddrBits(24), .isProgramMemory("true"), .Bits(8)) RAM_0 (
    .A(A[23:0]), .Din(Din[31:24]), .str(multiplexer_3_out), .C(C), .ld(ld), .D(D[31:24]));

  // Notes on the sheet:
  //   A: default 8192
  //   StoreWHB: 00 Store Word
  //   01 Store Half (Word)
  //   11 Store Byte
  //   00 Word
  //   10 Half (Word)
  //   11 Byte
endmodule
