// Digital circuit new_ALU.dig as structural Verilog
module new_ALU (
  input  [2:0] ALUControl,
  input  [31:0] A,
  input  [31:0] B,
  output [31:0] OUT,
  output [3:0] NZCV_Flags
);

  wire _16bit_carry_lookahead_adder_1_co, _16bit_carry_lookahead_adder_2_co, not_1_out, or_1_out, or_2_out,
       or_3_out, or_4_out, or_5_out, or_6_out, or_7_out, or_8_out, or_9_out, or_10_out, xnor_1_out, xor_1_out;
  wire [0:0] SLT, SLTU;
  wire [30:0] Y;
  wire [31:0] AND, ARITHSHIFT, LSHIFT, OR, RSHIFT, XOR;

  // Probe OUT on OUT
  r_shift r_shift_1 (.Input(A), .Shift(B), .Y(RSHIFT));
  arith_shift arith_shift_1 (.Input(A), .Shift(B), .Y(ARITHSHIFT));
  l_shift l_shift_1 (.Input(A), .Shift(B), .Y(LSHIFT));
  _8_xor _8_xor_1 (.A(A[7:0]), .B(B[7:0]), .Y(XOR[7:0]));
  _8_xor _8_xor_2 (.A(A[15:8]), .B(B[15:8]), .Y(XOR[15:8]));
  _8_xor _8_xor_3 (.A(A[23:16]), .B(B[23:16]), .Y(XOR[23:16]));
  _8_xor _8_xor_4 (.A(A[31:24]), .B(B[31:24]), .Y(XOR[31:24]));
  _8_or _8_or_1 (.A(A[7:0]), .B(B[7:0]), .Y(OR[7:0]));
  _8_or _8_or_2 (.A(A[15:8]), .B(B[15:8]), .Y(OR[15:8]));
  _8_or _8_or_3 (.A(A[23:16]), .B(B[23:16]), .Y(OR[23:16]));
  _8_or _8_or_4 (.A(A[31:24]), .B(B[31:24]), .Y(OR[31:24]));
  _8_and _8_and_1 (.A(A[7:0]), .B(B[7:0]), .Y(AND[7:0]));
  _8_and _8_and_2 (.A(A[15:8]), .B(B[15:8]), .Y(AND[15:8]));
  _8_and _8_and_3 (.A(A[23:16]), .B(B[23:16]), .Y(AND[23:16]));
  _8_and _8_and_4 (.A(A[31:24]), .B(B[31:24]), .Y(AND[31:24]));
  _16bit_carry_lookahead_adder _16bit_carry_lookahead_adder_1 (
    .A(A[15:0]), .B(B[15:0]), .subtract(ALUControl[0]), .Ci(ALUControl[0]), .S(Y[15:0]),
    .Co(_16bit_carry_lookahead_adder_1_co));
  _16bit_carry_lookahead_adder _16bit_carry_lookahead_adder_2 (
    .A(A[31:16]), .B(B[31:16]), .subtract(ALUControl[0]), .Ci(_16bit_carry_lookahead_adder_1_co),
    .S({NZCV_Flags[0], Y[30:16]}), .Co(_16bit_carry_lookahead_adder_2_co));
  Multiplexer #(.Selector_Bits(3), .Bits(32)) multiplexer_1 (
    .sel(ALUControl), .in_0({NZCV_Flags[0], Y}), .in_1({NZCV_Flags[0], Y}), .in_2(AND), .in_3(OR),
    .in_4({{31{1'b0}}, SLTU[0]}), .in_5({{31{1'b0}}, SLT[0]}), .in_6(LSHIFT), .in_7(XOR), .out(OUT));
  // Probe on {NZCV_Flags[0], Y}
  xor xor_1 (xor_1_out, NZCV_Flags[0], A[31]);
  or or_1 (or_1_out, Y[0], Y[1], Y[2], Y[3]);
  or or_2 (or_2_out, Y[4], Y[5], Y[6], Y[7]);
  or or_3 (or_3_out, Y[8], Y[9], Y[10], Y[11]);
  or or_4 (or_4_out, Y[12], Y[13], Y[14], Y[15]);
  or or_5 (or_5_out, Y[16], Y[17], Y[18], Y[19]);
  or or_6 (or_6_out, Y[20], Y[21], Y[22], Y[23]);
  or or_7 (or_7_out, Y[24], Y[25], Y[26], Y[27]);
  or or_8 (or_8_out, Y[28], Y[29], Y[30], NZCV_Flags[0]);
  xnor xnor_1 (xnor_1_out, B[31], A[31]);
  not not_1 (not_1_out, ALUControl[1]);
  and and_1 (NZCV_Flags[2], not_1_out, _16bit_carry_lookahead_adder_2_co);
  or or_9 (or_9_out, or_1_out, or_2_out, or_3_out, or_4_out);
  or or_10 (or_10_out, or_5_out, or_6_out, or_7_out, or_8_out);
  and and_2 (NZCV_Flags[3], xnor_1_out, xor_1_out, not_1_out);
  nor nor_1 (SLTU[0], _16bit_carry_lookahead_adder_2_co, NZCV_Flags[1]);
  nor nor_2 (NZCV_Flags[1], or_9_out, or_10_out);
  xor xor_2 (SLT[0], NZCV_Flags[3], NZCV_Flags[0]);
  // Probe on {{31{1'b0}}, SLT[0]}

  // Other names for the same wires on the sheet: negative = NZCV_Flags[0]; Y[31] = NZCV_Flags[0]; A_31 = A[31];
  //   ALU[2:0] = ALUControl; ALU_0 = ALUControl[0]; ALU_1 = ALUControl[1]; ALU_2 = ALUControl[2]; B_31 = B[31];
  //   carry = NZCV_Flags[2]; overflow = NZCV_Flags[3]; zero = NZCV_Flags[1]

  // Notes on the sheet:
  //   000 ADD
  //   001 SUB
  //   010 AND
  //   011 OR
  //   100 SET LESS THAN UNSIGNED A<B
  //   101 Set Less than A<B
  //   110 SHIFT LEFT LOGICAL
  //   111 XOR
  //   Output Flag
  //   1000 N Negative
  //   0100 Z Zero
  //   0010 C Carry
  //   0001 V Overflow
endmodule
