// Digital circuit o_operator.dig as structural Verilog
module o_operator (
  input  g__in,
  input  p__in,
  input  g_in,
  input  p_in,
  output g,
  output p
);

  wire and_1_out;

  and and_1 (and_1_out, g__in, p_in);
  and and_2 (p, p_in, p__in);
  or or_1 (g, g_in, and_1_out);
endmodule
