// Digital circuit r_shift.dig as structural Verilog
module r_shift (
  input  [31:0] Input,
  input  [31:0] Shift,
  output [31:0] Y
);

  BarrelShifter #(.Bits(32), .barrelSigned("true"), .direction("right")) Shift_R (
    .in(Input), .shift(Shift[6:0]), .out(Y));
endmodule
